// Logisim project maquinaDeEstadosUC.circ as structural Verilog: 1 circuit, main circuit main
module main (
  input  OP,
  input  Reset
);

  wire and_1_out, and_2_out, and_3_out, and_4_out, and_5_out, clock_1_out, d_ff_1_qn, d_ff_2_qn, d_ff_3_qn,
       not_1_out, or_1_out;
  wire [2:0] d_ff_3_q;

  Clock clock_1 (.out(clock_1_out));
  not not_1 (not_1_out, OP);
  D_Flip_Flop d_ff_1 (
    .D(and_2_out), .clk(clock_1_out), .Q(d_ff_3_q[2]), .Qn(d_ff_1_qn), .reset(Reset));  // open: preset
  D_Flip_Flop d_ff_2 (.D(or_1_out), .clk(clock_1_out), .Q(d_ff_3_q[1]), .Qn(d_ff_2_qn), .reset(Reset));  // open: preset
  D_Flip_Flop d_ff_3 (
    .D(and_1_out), .clk(clock_1_out), .Q(d_ff_3_q[0]), .Qn(d_ff_3_qn), .reset(Reset));  // open: preset
  // BCD_to_7_Segment_decoder bcd_to_7_segment_decoder_1: pin names not known; wires that end beside it: {1'b0, d_ff_3_q}
  _7_Segment_Display u_7_segment_display_1 ();  // open: g, f, a, b, e, d, c, dp
  and and_1 (and_1_out, d_ff_1_qn, d_ff_3_qn);
  and and_2 (and_2_out, not_1_out, and_5_out);
  and and_3 (and_3_out, d_ff_3_q[1], d_ff_3_qn);
  and and_4 (and_4_out, OP, and_5_out);
  and and_5 (and_5_out, d_ff_1_qn, d_ff_2_qn, d_ff_3_q[0]);
  or or_1 (or_1_out, and_3_out, and_4_out);

  // Notes on the sheet:
  //   Q2
  //   Q1
  //   Q0
  //   LogicaD2
  //   LogicaD0
  //   estado atual
  //   logicaD1
  //   Sinal de estado S1
  //   a máquina está em S1(001)
endmodule
